# Fritzing sketch connections (saved by Fritzing 0.9.4)
breadboards: 1

parts:
  Mod1 = Raspberry Pi Pico
  S1 = Pushbutton [package="[SMD]"]
  SG1 = Buzzer 12mm [package=buzzer-12mm-ns]
  Part1 = MQ-9 breakout
  R1 = Resistor [tolerance=±5% resistance=150 package="0402 [SMD]"]
  D1 = Zener Diode [breakdown_voltage=3.3V package="Melf DO-213 AB [SMD]"]

nets:
  N1: Mod1.pin_1, R1.Pin_1, D1.cathode
  N2: Mod1.pin_2, SG1.1
  N3: Mod1.pin_3, Mod1.pin_8, Mod1.pin_13, Mod1.pin_18, Mod1.pin_23, Mod1.pin_28, Mod1.pin_33, Mod1.pin_38, SG1.2, Part1.GND, D1.anode
  N4: Mod1.pin_4, S1.Pin_1, S1.Pin_2
  N5: Mod1.pin_36, S1.Pin_3, S1.Pin_4
  N6: Mod1.pin_40, Part1.VCC
  N7: Part1.DO, R1.Pin_0

custom parts:
  Raspberry Pi Pico: Raspberry Pi Pico. Based around the RP2040 microcontroller the Pico is a low cost microcontroller device bringing Raspberry Pi quality, cost, and easy of use to the microcontroller space. Jan 2021, Split part in to two versions: tht (this one) and SMD. This one will drill holes for a .1 in header in pcb to allow plugging in the module as well as providing pads to solder the module to the top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
  MQ-9 breakout: SKU: 101284
